// Logisim project hw3.circ as structural Verilog: 12 circuits, main circuit hw3
module Full_Adder (
  input  Carry_IN,
  input  Input_1,
  input  Input_2,
  output Sum_Bit,
  output Carry_Out
);

  wire and_1_out, and_2_out, xor_1_out, xor_2_out;

  and and_1 (and_1_out, Input_2, Input_1);
  xor xor_1 (xor_1_out, Input_2, Input_1);
  and and_2 (and_2_out, xor_1_out, Carry_IN);
  xor xor_2 (xor_2_out, Input_1, Input_2);
  or or_1 (Carry_Out, and_1_out, and_2_out);
  xor xor_3 (Sum_Bit, Carry_IN, xor_2_out);
endmodule

// Adder
module _16_Bit_Adder (
  input  [15:0] Number_2,
  input  [15:0] Number_1,
  input  _0_to_Add_1_to_subtract,
  output Overflow,
  output [15:0] _16_Bit_Sum
);

  wire full_adder_1_carry_out, full_adder_2_carry_out, full_adder_3_carry_out, full_adder_4_carry_out,
       full_adder_5_carry_out, full_adder_6_carry_out, full_adder_7_carry_out, full_adder_8_carry_out,
       full_adder_9_carry_out, full_adder_10_carry_out, full_adder_11_carry_out, full_adder_12_carry_out,
       full_adder_13_carry_out, full_adder_14_carry_out, full_adder_15_carry_out, full_adder_16_carry_out,
       xor_1_out, xor_2_out, xor_3_out, xor_4_out, xor_5_out, xor_6_out, xor_7_out, xor_8_out, xor_9_out,
       xor_10_out, xor_11_out, xor_12_out, xor_13_out, xor_14_out, xor_15_out, xor_16_out;

  xor xor_1 (xor_1_out, _0_to_Add_1_to_subtract, Number_2[15]);
  xor xor_2 (xor_2_out, _0_to_Add_1_to_subtract, Number_2[14]);
  Full_Adder full_adder_1 (
    .Carry_IN(full_adder_2_carry_out), .Input_1(Number_1[15]), .Input_2(xor_1_out),
    .Sum_Bit(_16_Bit_Sum[15]), .Carry_Out(full_adder_1_carry_out));
  Full_Adder full_adder_2 (
    .Carry_IN(full_adder_4_carry_out), .Input_1(Number_1[14]), .Input_2(xor_2_out),
    .Sum_Bit(_16_Bit_Sum[14]), .Carry_Out(full_adder_2_carry_out));
  xor xor_3 (xor_3_out, _0_to_Add_1_to_subtract, Number_2[13]);
  xor xor_4 (xor_4_out, _0_to_Add_1_to_subtract, Number_2[12]);
  Full_Adder full_adder_3 (
    .Carry_IN(full_adder_5_carry_out), .Input_1(Number_1[12]), .Input_2(xor_4_out),
    .Sum_Bit(_16_Bit_Sum[12]), .Carry_Out(full_adder_3_carry_out));
  Full_Adder full_adder_4 (
    .Carry_IN(full_adder_3_carry_out), .Input_1(Number_1[13]), .Input_2(xor_3_out),
    .Sum_Bit(_16_Bit_Sum[13]), .Carry_Out(full_adder_4_carry_out));
  xor xor_5 (xor_5_out, _0_to_Add_1_to_subtract, Number_2[11]);
  Full_Adder full_adder_5 (
    .Carry_IN(full_adder_6_carry_out), .Input_1(Number_1[11]), .Input_2(xor_5_out),
    .Sum_Bit(_16_Bit_Sum[11]), .Carry_Out(full_adder_5_carry_out));
  xor xor_6 (xor_6_out, _0_to_Add_1_to_subtract, Number_2[9]);
  xor xor_7 (xor_7_out, _0_to_Add_1_to_subtract, Number_2[10]);
  Full_Adder full_adder_6 (
    .Carry_IN(full_adder_7_carry_out), .Input_1(Number_1[10]), .Input_2(xor_7_out),
    .Sum_Bit(_16_Bit_Sum[10]), .Carry_Out(full_adder_6_carry_out));
  Full_Adder full_adder_7 (
    .Carry_IN(full_adder_8_carry_out), .Input_1(Number_1[9]), .Input_2(xor_6_out), .Sum_Bit(_16_Bit_Sum[9]),
    .Carry_Out(full_adder_7_carry_out));
  xor xor_8 (xor_8_out, _0_to_Add_1_to_subtract, Number_2[7]);
  xor xor_9 (xor_9_out, _0_to_Add_1_to_subtract, Number_2[8]);
  Full_Adder full_adder_8 (
    .Carry_IN(full_adder_9_carry_out), .Input_1(Number_1[8]), .Input_2(xor_9_out), .Sum_Bit(_16_Bit_Sum[8]),
    .Carry_Out(full_adder_8_carry_out));
  xor xor_10 (xor_10_out, _0_to_Add_1_to_subtract, Number_2[6]);
  Full_Adder full_adder_9 (
    .Carry_IN(full_adder_10_carry_out), .Input_1(Number_1[7]), .Input_2(xor_8_out), .Sum_Bit(_16_Bit_Sum[7]),
    .Carry_Out(full_adder_9_carry_out));
  Full_Adder full_adder_10 (
    .Carry_IN(full_adder_11_carry_out), .Input_1(Number_1[6]), .Input_2(xor_10_out),
    .Sum_Bit(_16_Bit_Sum[6]), .Carry_Out(full_adder_10_carry_out));
  xor xor_11 (xor_11_out, _0_to_Add_1_to_subtract, Number_2[4]);
  xor xor_12 (xor_12_out, _0_to_Add_1_to_subtract, Number_2[5]);
  Full_Adder full_adder_11 (
    .Carry_IN(full_adder_12_carry_out), .Input_1(Number_1[5]), .Input_2(xor_12_out),
    .Sum_Bit(_16_Bit_Sum[5]), .Carry_Out(full_adder_11_carry_out));
  Full_Adder full_adder_12 (
    .Carry_IN(full_adder_13_carry_out), .Input_1(Number_1[4]), .Input_2(xor_11_out),
    .Sum_Bit(_16_Bit_Sum[4]), .Carry_Out(full_adder_12_carry_out));
  xor xor_13 (xor_13_out, _0_to_Add_1_to_subtract, Number_2[3]);
  Full_Adder full_adder_13 (
    .Carry_IN(full_adder_15_carry_out), .Input_1(Number_1[3]), .Input_2(xor_13_out),
    .Sum_Bit(_16_Bit_Sum[3]), .Carry_Out(full_adder_13_carry_out));
  xor xor_14 (xor_14_out, _0_to_Add_1_to_subtract, Number_2[2]);
  xor xor_15 (xor_15_out, _0_to_Add_1_to_subtract, Number_2[1]);
  Full_Adder full_adder_14 (
    .Carry_IN(full_adder_16_carry_out), .Input_1(Number_1[1]), .Input_2(xor_15_out),
    .Sum_Bit(_16_Bit_Sum[1]), .Carry_Out(full_adder_14_carry_out));
  Full_Adder full_adder_15 (
    .Carry_IN(full_adder_14_carry_out), .Input_1(Number_1[2]), .Input_2(xor_14_out),
    .Sum_Bit(_16_Bit_Sum[2]), .Carry_Out(full_adder_15_carry_out));
  xor xor_16 (xor_16_out, _0_to_Add_1_to_subtract, Number_2[0]);
  Full_Adder full_adder_16 (
    .Carry_IN(_0_to_Add_1_to_subtract), .Input_1(Number_1[0]), .Input_2(xor_16_out),
    .Sum_Bit(_16_Bit_Sum[0]), .Carry_Out(full_adder_16_carry_out));
endmodule

// And
module _16_Bit_And (
  input  [15:0] Number_2,
  input  [15:0] Number_1,
  output [15:0] _16_Bit_And
);

  and and_1 (_16_Bit_And[14], Number_2[14], Number_1[14]);
  and and_2 (_16_Bit_And[15], Number_2[15], Number_1[15]);
  and and_3 (_16_Bit_And[13], Number_2[13], Number_1[13]);
  and and_4 (_16_Bit_And[12], Number_2[12], Number_1[12]);
  and and_5 (_16_Bit_And[11], Number_2[11], Number_1[11]);
  and and_6 (_16_Bit_And[10], Number_2[10], Number_1[10]);
  and and_7 (_16_Bit_And[9], Number_2[9], Number_1[9]);
  and and_8 (_16_Bit_And[8], Number_2[8], Number_1[8]);
  and and_9 (_16_Bit_And[7], Number_2[7], Number_1[7]);
  and and_10 (_16_Bit_And[6], Number_2[6], Number_1[6]);
  and and_11 (_16_Bit_And[4], Number_2[4], Number_1[4]);
  and and_12 (_16_Bit_And[5], Number_2[5], Number_1[5]);
  and and_13 (_16_Bit_And[2], Number_2[2], Number_1[2]);
  and and_14 (_16_Bit_And[3], Number_2[3], Number_1[3]);
  and and_15 (_16_Bit_And[1], Number_2[1], Number_1[1]);
  and and_16 (_16_Bit_And[0], Number_2[0], Number_1[0]);
endmodule

// OR
module _16_Bit_OR (
  input  [15:0] Number_2,
  input  [15:0] Number_1,
  output [15:0] _16_Bit_OR
);

  or or_1 (_16_Bit_OR[14], Number_2[14], Number_1[14]);
  or or_2 (_16_Bit_OR[15], Number_2[15], Number_1[15]);
  or or_3 (_16_Bit_OR[13], Number_2[13], Number_1[13]);
  or or_4 (_16_Bit_OR[11], Number_2[11], Number_1[11]);
  or or_5 (_16_Bit_OR[12], Number_2[12], Number_1[12]);
  or or_6 (_16_Bit_OR[10], Number_2[10], Number_1[10]);
  or or_7 (_16_Bit_OR[9], Number_2[9], Number_1[9]);
  or or_8 (_16_Bit_OR[8], Number_2[8], Number_1[8]);
  or or_9 (_16_Bit_OR[7], Number_2[7], Number_1[7]);
  or or_10 (_16_Bit_OR[6], Number_2[6], Number_1[6]);
  or or_11 (_16_Bit_OR[5], Number_2[5], Number_1[5]);
  or or_12 (_16_Bit_OR[4], Number_2[4], Number_1[4]);
  or or_13 (_16_Bit_OR[2], Number_2[2], Number_1[2]);
  or or_14 (_16_Bit_OR[3], Number_2[3], Number_1[3]);
  or or_15 (_16_Bit_OR[1], Number_2[1], Number_1[1]);
  or or_16 (_16_Bit_OR[0], Number_2[0], Number_1[0]);
endmodule

// LSL
module n_bit_lsl (
  input  [3:0] Number_of_shifts,
  input  [15:0] Input,
  output [15:0] Shifted_Value
);

  wire [15:0] left_shift_logical_1_left_shifted_value, left_shift_logical_2_left_shifted_value,
       left_shift_logical_3_left_shifted_value, left_shift_logical_4_left_shifted_value,
       left_shift_logical_5_left_shifted_value, left_shift_logical_6_left_shifted_value,
       left_shift_logical_7_left_shifted_value, left_shift_logical_8_left_shifted_value,
       left_shift_logical_9_left_shifted_value, left_shift_logical_10_left_shifted_value,
       left_shift_logical_11_left_shifted_value, left_shift_logical_12_left_shifted_value,
       left_shift_logical_13_left_shifted_value, left_shift_logical_14_left_shifted_value,
       left_shift_logical_15_left_shifted_value;

  Left_Shift_Logical left_shift_logical_1 (.Input(Input), .left_shifted_value(left_shift_logical_1_left_shifted_value));
  Left_Shift_Logical left_shift_logical_2 (
    .Input(left_shift_logical_1_left_shifted_value),
    .left_shifted_value(left_shift_logical_2_left_shifted_value));
  Left_Shift_Logical left_shift_logical_3 (
    .Input(left_shift_logical_4_left_shifted_value),
    .left_shifted_value(left_shift_logical_3_left_shifted_value));
  Left_Shift_Logical left_shift_logical_4 (
    .Input(left_shift_logical_2_left_shifted_value),
    .left_shifted_value(left_shift_logical_4_left_shifted_value));
  Left_Shift_Logical left_shift_logical_5 (
    .Input(left_shift_logical_3_left_shifted_value),
    .left_shifted_value(left_shift_logical_5_left_shifted_value));
  Left_Shift_Logical left_shift_logical_6 (
    .Input(left_shift_logical_7_left_shifted_value),
    .left_shifted_value(left_shift_logical_6_left_shifted_value));
  Left_Shift_Logical left_shift_logical_7 (
    .Input(left_shift_logical_5_left_shifted_value),
    .left_shifted_value(left_shift_logical_7_left_shifted_value));
  Left_Shift_Logical left_shift_logical_8 (
    .Input(left_shift_logical_9_left_shifted_value),
    .left_shifted_value(left_shift_logical_8_left_shifted_value));
  Left_Shift_Logical left_shift_logical_9 (
    .Input(left_shift_logical_6_left_shifted_value),
    .left_shifted_value(left_shift_logical_9_left_shifted_value));
  Left_Shift_Logical left_shift_logical_10 (
    .Input(left_shift_logical_8_left_shifted_value),
    .left_shifted_value(left_shift_logical_10_left_shifted_value));
  Left_Shift_Logical left_shift_logical_11 (
    .Input(left_shift_logical_12_left_shifted_value),
    .left_shifted_value(left_shift_logical_11_left_shifted_value));
  Left_Shift_Logical left_shift_logical_12 (
    .Input(left_shift_logical_10_left_shifted_value),
    .left_shifted_value(left_shift_logical_12_left_shifted_value));
  Left_Shift_Logical left_shift_logical_13 (
    .Input(left_shift_logical_11_left_shifted_value),
    .left_shifted_value(left_shift_logical_13_left_shifted_value));
  Multiplexer #(.select(4), .width(16)) multiplexer_1 (
    .in0(Input), .in1(left_shift_logical_1_left_shifted_value),
    .in2(left_shift_logical_2_left_shifted_value), .in3(left_shift_logical_4_left_shifted_value),
    .in4(left_shift_logical_3_left_shifted_value), .in5(left_shift_logical_5_left_shifted_value),
    .in6(left_shift_logical_7_left_shifted_value), .in7(left_shift_logical_6_left_shifted_value),
    .in8(left_shift_logical_9_left_shifted_value), .in9(left_shift_logical_8_left_shifted_value),
    .in10(left_shift_logical_10_left_shifted_value), .in11(left_shift_logical_12_left_shifted_value),
    .in12(left_shift_logical_11_left_shifted_value), .in13(left_shift_logical_13_left_shifted_value),
    .in14(left_shift_logical_15_left_shifted_value), .in15(left_shift_logical_14_left_shifted_value),
    .out(Shifted_Value), .sel(Number_of_shifts), .en(1'b1));
  Left_Shift_Logical left_shift_logical_14 (
    .Input(left_shift_logical_15_left_shifted_value),
    .left_shifted_value(left_shift_logical_14_left_shifted_value));
  Left_Shift_Logical left_shift_logical_15 (
    .Input(left_shift_logical_13_left_shifted_value),
    .left_shifted_value(left_shift_logical_15_left_shifted_value));
endmodule

module Left_Shift_Logical (
  input  [15:0] Input,
  output [15:0] left_shifted_value
);


  assign left_shifted_value = {Input[14:0], 1'b0};
endmodule

module Arthimetic_Right_Shift (
  input  [15:0] Input,
  output [15:0] Output
);


  assign Output = {{2{Input[15]}}, Input[14:1]};
  // also tied to GND on the sheet: Input[0]
endmodule

// ASR
module n_bit_asr (
  input  [3:0] Number_of_right_shifts,
  input  [15:0] Input,
  output [15:0] Output
);

  wire [15:0] arthimetic_right_shift_1_output, arthimetic_right_shift_2_output,
       arthimetic_right_shift_3_output, arthimetic_right_shift_4_output, arthimetic_right_shift_5_output,
       arthimetic_right_shift_6_output, arthimetic_right_shift_7_output, arthimetic_right_shift_8_output,
       arthimetic_right_shift_9_output, arthimetic_right_shift_10_output, arthimetic_right_shift_11_output,
       arthimetic_right_shift_12_output, arthimetic_right_shift_13_output, arthimetic_right_shift_14_output,
       arthimetic_right_shift_15_output;

  Arthimetic_Right_Shift arthimetic_right_shift_1 (
    .Output(arthimetic_right_shift_1_output), .Input(arthimetic_right_shift_2_output));
  Arthimetic_Right_Shift arthimetic_right_shift_2 (.Output(arthimetic_right_shift_2_output), .Input(Input));
  Arthimetic_Right_Shift arthimetic_right_shift_3 (
    .Output(arthimetic_right_shift_3_output), .Input(arthimetic_right_shift_1_output));
  Arthimetic_Right_Shift arthimetic_right_shift_4 (
    .Output(arthimetic_right_shift_4_output), .Input(arthimetic_right_shift_5_output));
  Arthimetic_Right_Shift arthimetic_right_shift_5 (
    .Output(arthimetic_right_shift_5_output), .Input(arthimetic_right_shift_3_output));
  Arthimetic_Right_Shift arthimetic_right_shift_6 (
    .Output(arthimetic_right_shift_6_output), .Input(arthimetic_right_shift_4_output));
  Arthimetic_Right_Shift arthimetic_right_shift_7 (
    .Output(arthimetic_right_shift_7_output), .Input(arthimetic_right_shift_8_output));
  Arthimetic_Right_Shift arthimetic_right_shift_8 (
    .Output(arthimetic_right_shift_8_output), .Input(arthimetic_right_shift_6_output));
  Arthimetic_Right_Shift arthimetic_right_shift_9 (
    .Output(arthimetic_right_shift_9_output), .Input(arthimetic_right_shift_10_output));
  Arthimetic_Right_Shift arthimetic_right_shift_10 (
    .Output(arthimetic_right_shift_10_output), .Input(arthimetic_right_shift_7_output));
  Arthimetic_Right_Shift arthimetic_right_shift_11 (
    .Output(arthimetic_right_shift_11_output), .Input(arthimetic_right_shift_9_output));
  Arthimetic_Right_Shift arthimetic_right_shift_12 (
    .Output(arthimetic_right_shift_12_output), .Input(arthimetic_right_shift_13_output));
  Arthimetic_Right_Shift arthimetic_right_shift_13 (
    .Output(arthimetic_right_shift_13_output), .Input(arthimetic_right_shift_11_output));
  Arthimetic_Right_Shift arthimetic_right_shift_14 (
    .Output(arthimetic_right_shift_14_output), .Input(arthimetic_right_shift_12_output));
  Arthimetic_Right_Shift arthimetic_right_shift_15 (
    .Output(arthimetic_right_shift_15_output), .Input(arthimetic_right_shift_14_output));
  Multiplexer #(.select(4), .width(16)) multiplexer_1 (
    .in0(Input), .in1(arthimetic_right_shift_2_output), .in2(arthimetic_right_shift_1_output),
    .in3(arthimetic_right_shift_3_output), .in4(arthimetic_right_shift_5_output),
    .in5(arthimetic_right_shift_4_output), .in6(arthimetic_right_shift_6_output),
    .in7(arthimetic_right_shift_8_output), .in8(arthimetic_right_shift_7_output),
    .in9(arthimetic_right_shift_10_output), .in10(arthimetic_right_shift_9_output),
    .in11(arthimetic_right_shift_11_output), .in12(arthimetic_right_shift_13_output),
    .in13(arthimetic_right_shift_12_output), .in14(arthimetic_right_shift_14_output),
    .in15(arthimetic_right_shift_15_output), .out(Output), .sel(Number_of_right_shifts), .en(1'b1));
endmodule

module ALU (
  input  [15:0] rs,
  input  [15:0] rt,
  input  [3:0] _0_3,
  input  [3:0] Opcode,
  output [15:0] Output
);

  wire [15:0] n16_bit_adder_1__16_bit_sum, n16_bit_adder_2__16_bit_sum, n16_bit_and_1__16_bit_and,
       n16_bit_or_1__16_bit_or, n_bit_asr_1_output, n_bit_lsl_1_shifted_value;

  _16_Bit_Adder u_16_bit_adder_1 (
    .Number_2(rt), ._0_to_Add_1_to_subtract(1'b0), .Number_1(rs), ._16_Bit_Sum(n16_bit_adder_1__16_bit_sum));  // open: Overflow
  _16_Bit_Adder u_16_bit_adder_2 (
    .Number_2(rt), ._0_to_Add_1_to_subtract(1'b1), .Number_1(rs), ._16_Bit_Sum(n16_bit_adder_2__16_bit_sum));  // open: Overflow
  _16_Bit_And u_16_bit_and_1 (.Number_2(rt), .Number_1(rs), ._16_Bit_And(n16_bit_and_1__16_bit_and));
  _16_Bit_OR u_16_bit_or_1 (.Number_2(rt), .Number_1(rs), ._16_Bit_OR(n16_bit_or_1__16_bit_or));
  n_bit_lsl n_bit_lsl_1 (.Input(rs), .Number_of_shifts(_0_3), .Shifted_Value(n_bit_lsl_1_shifted_value));
  n_bit_asr n_bit_asr_1 (.Input(rs), .Number_of_right_shifts(_0_3), .Output(n_bit_asr_1_output));
  Multiplexer #(.select(4), .width(16)) multiplexer_1 (
    .in1(n16_bit_adder_1__16_bit_sum), .in3(n16_bit_and_1__16_bit_and), .in5(n_bit_lsl_1_shifted_value),
    .in12(n16_bit_or_1__16_bit_or), .in13(n_bit_asr_1_output), .in14(n16_bit_adder_2__16_bit_sum),
    .out(Output), .sel(Opcode), .en(1'b1));  // open: in0, in2, in4, in6, in7, in8, in9, in10, in11, in15
endmodule

// Registers
module Register_File (
  input  [3:0] rd___Write_Back_Register,
  input  Write,
  input  [15:0] Write_Data,
  input  Clock,
  input  Asynchronous_Clear,
  input  [3:0] rs,
  input  [3:0] rt,
  output [15:0] Output_of_rs,
  output [15:0] Output_of_rt
);

  wire and_1_out, and_2_out, and_3_out, and_4_out, and_5_out, and_6_out, and_7_out, and_8_out, and_9_out,
       and_10_out, and_11_out, and_12_out, and_13_out, and_14_out, and_15_out, and_16_out;
  wire [15:0] n_bit_lsl_1_shifted_value, register_1_q, register_2_q, register_3_q, register_4_q,
       register_5_q, register_6_q, register_7_q, register_8_q, register_9_q, register_10_q, register_11_q,
       register_12_q, register_13_q, register_14_q, register_15_q, register_16_q;

  and and_1 (and_1_out, n_bit_lsl_1_shifted_value[0], Write);
  and and_2 (and_2_out, n_bit_lsl_1_shifted_value[1], Write);
  Register #(.width(16)) register_1 (
    .D(Write_Data), .en(and_1_out), .Q(register_1_q), .clk(Clock), .clr(Asynchronous_Clear));
  and and_3 (and_3_out, n_bit_lsl_1_shifted_value[2], Write);
  Register #(.width(16)) register_2 (
    .D(Write_Data), .en(and_2_out), .Q(register_2_q), .clk(Clock), .clr(Asynchronous_Clear));
  and and_4 (and_4_out, n_bit_lsl_1_shifted_value[3], Write);
  and and_5 (and_5_out, n_bit_lsl_1_shifted_value[4], Write);
  Register #(.width(16)) register_3 (
    .D(Write_Data), .en(and_3_out), .Q(register_3_q), .clk(Clock), .clr(Asynchronous_Clear));
  Register #(.width(16)) register_4 (
    .D(Write_Data), .en(and_4_out), .Q(register_4_q), .clk(Clock), .clr(Asynchronous_Clear));
  and and_6 (and_6_out, n_bit_lsl_1_shifted_value[5], Write);
  Register #(.width(16)) register_5 (
    .D(Write_Data), .en(and_5_out), .Q(register_5_q), .clk(Clock), .clr(Asynchronous_Clear));
  and and_7 (and_7_out, n_bit_lsl_1_shifted_value[6], Write);
  Register #(.width(16)) register_6 (
    .D(Write_Data), .en(and_6_out), .Q(register_6_q), .clk(Clock), .clr(Asynchronous_Clear));
  Multiplexer #(.select(4), .width(16)) multiplexer_1 (
    .in0(register_1_q), .in1(register_2_q), .in2(register_3_q), .in3(register_4_q), .in4(register_5_q),
    .in5(register_6_q), .in6(register_7_q), .in7(register_8_q), .in8(register_9_q), .in9(register_10_q),
    .in10(register_11_q), .in11(register_12_q), .in12(register_13_q), .in13(register_14_q),
    .in14(register_15_q), .in15(register_16_q), .out(Output_of_rs), .sel(rs), .en(1'b1));
  Multiplexer #(.select(4), .width(16)) multiplexer_2 (
    .in0(register_1_q), .in1(register_2_q), .in2(register_3_q), .in3(register_4_q), .in4(register_5_q),
    .in5(register_6_q), .in6(register_7_q), .in7(register_8_q), .in8(register_9_q), .in9(register_10_q),
    .in10(register_11_q), .in11(register_12_q), .in12(register_13_q), .in13(register_14_q),
    .in14(register_15_q), .in15(register_16_q), .out(Output_of_rt), .sel(rt), .en(1'b1));
  n_bit_lsl n_bit_lsl_1 (
    .Input(16'h1), .Number_of_shifts(rd___Write_Back_Register), .Shifted_Value(n_bit_lsl_1_shifted_value));
  and and_8 (and_8_out, n_bit_lsl_1_shifted_value[7], Write);
  and and_9 (and_9_out, n_bit_lsl_1_shifted_value[8], Write);
  Register #(.width(16)) register_7 (
    .D(Write_Data), .en(and_7_out), .Q(register_7_q), .clk(Clock), .clr(Asynchronous_Clear));
  Register #(.width(16)) register_8 (
    .D(Write_Data), .en(and_8_out), .Q(register_8_q), .clk(Clock), .clr(Asynchronous_Clear));
  and and_10 (and_10_out, n_bit_lsl_1_shifted_value[9], Write);
  Register #(.width(16)) register_9 (
    .D(Write_Data), .en(and_9_out), .Q(register_9_q), .clk(Clock), .clr(Asynchronous_Clear));
  and and_11 (and_11_out, n_bit_lsl_1_shifted_value[10], Write);
  Register #(.width(16)) register_10 (
    .D(Write_Data), .en(and_10_out), .Q(register_10_q), .clk(Clock), .clr(Asynchronous_Clear));
  and and_12 (and_12_out, n_bit_lsl_1_shifted_value[12], Write);
  and and_13 (and_13_out, n_bit_lsl_1_shifted_value[11], Write);
  Register #(.width(16)) register_11 (
    .D(Write_Data), .en(and_11_out), .Q(register_11_q), .clk(Clock), .clr(Asynchronous_Clear));
  Register #(.width(16)) register_12 (
    .D(Write_Data), .en(and_13_out), .Q(register_12_q), .clk(Clock), .clr(Asynchronous_Clear));
  and and_14 (and_14_out, n_bit_lsl_1_shifted_value[13], Write);
  Register #(.width(16)) register_13 (
    .D(Write_Data), .en(and_12_out), .Q(register_13_q), .clk(Clock), .clr(Asynchronous_Clear));
  and and_15 (and_15_out, n_bit_lsl_1_shifted_value[14], Write);
  Register #(.width(16)) register_14 (
    .D(Write_Data), .en(and_14_out), .Q(register_14_q), .clk(Clock), .clr(Asynchronous_Clear));
  and and_16 (and_16_out, n_bit_lsl_1_shifted_value[15], Write);
  Register #(.width(16)) register_15 (
    .D(Write_Data), .en(and_15_out), .Q(register_15_q), .clk(Clock), .clr(Asynchronous_Clear));
  Register #(.width(16)) register_16 (
    .D(Write_Data), .en(and_16_out), .Q(register_16_q), .clk(Clock), .clr(Asynchronous_Clear));
endmodule

module Contol_Unit (
  input  Op3,
  input  Op2,
  input  Op1,
  input  Op0,
  output WReg,
  output RMem,
  output WMem,
  output Mux1,
  output Mux2
);

  wire and_1_out, and_2_out, and_3_out, and_4_out, and_5_out, not_1_out, not_2_out, not_3_out, not_4_out,
       not_5_out, not_6_out, not_7_out, not_8_out, not_9_out;

  not not_1 (not_1_out, Op3);
  and and_1 (and_1_out, not_1_out, Op0);
  and and_2 (and_2_out, Op3, Op2);
  not not_2 (not_2_out, Op3);
  not not_3 (not_3_out, Op2);
  not not_4 (not_4_out, Op1);
  not not_5 (not_5_out, Op0);
  not not_6 (not_6_out, Op3);
  not not_7 (not_7_out, Op3);
  and and_3 (and_3_out, not_7_out, Op0);
  and and_4 (and_4_out, Op2, not_8_out, Op0);
  not not_8 (not_8_out, Op1);
  and and_5 (and_5_out, Op3, Op2, not_9_out);
  not not_9 (not_9_out, Op0);
  or or_1 (WReg, and_1_out, and_2_out);
  and and_6 (RMem, not_2_out, Op2, Op1, Op0);
  and and_7 (WMem, Op3, not_3_out, not_4_out, not_5_out);
  and and_8 (Mux1, not_6_out, Op2, Op1, Op0);
  or or_2 (Mux2, and_3_out, and_4_out, and_5_out);
endmodule

module hw3 (
  input  in_1,
  input  in_2,
  input  [7:0] in_3,
  input  in_4,
  input  in_5,
  output out_6
);

  wire clock_1_out, contol_unit_1_mux1, contol_unit_1_mux2, contol_unit_1_rmem, contol_unit_1_wmem,
       contol_unit_1_wreg;
  wire [3:0] multiplexer_1_out, rom_1_data, rom_1_data_3;
  wire [7:0] counter_1_q;
  wire [15:0] alu_1_output, multiplexer_2_out, multiplexer_3_out, ram_1_data, register_file_1_output_of_rs,
       register_file_1_output_of_rt, rom_1_data_2;

  Counter counter_1 (
    .load(in_2), .D(in_3), .count(1'b1), .Q(counter_1_q), .carry(out_6), .clk(clock_1_out), .clr(in_4));
  Clock clock_1 (.out(clock_1_out));
  Contol_Unit contol_unit_1 (
    .Op3(rom_1_data_2[15]), .Op2(rom_1_data_2[14]), .Op1(rom_1_data_2[13]), .Op0(rom_1_data_2[12]),
    .WReg(contol_unit_1_wreg), .RMem(contol_unit_1_rmem), .WMem(contol_unit_1_wmem),
    .Mux1(contol_unit_1_mux1), .Mux2(contol_unit_1_mux2));
  Multiplexer #(.select(4), .width(4), .enable("false")) multiplexer_1 (
    .in1(rom_1_data_2[3:0]), .in3(rom_1_data_2[3:0]), .in5(rom_1_data_3), .in7(rom_1_data), .in8(rom_1_data),
    .in12(rom_1_data_2[3:0]), .in13(rom_1_data_3), .in14(rom_1_data_2[3:0]), .in15(rom_1_data),
    .out(multiplexer_1_out), .sel(rom_1_data_2[15:12]));  // open: in0, in2, in4, in6, in9, in10, in11
  ROM #(.dataWidth(16)) rom_1 (
    .addr(counter_1_q), .data({rom_1_data_2[15:12], rom_1_data, rom_1_data_3, rom_1_data_2[3:0]}));  // open: sel
  Register_File register_file_1 (
    .Clock(clock_1_out), .rs(rom_1_data), .rt(rom_1_data_3), .Write(contol_unit_1_wreg),
    .Asynchronous_Clear(in_1), .rd___Write_Back_Register(multiplexer_1_out),
    .Output_of_rs(register_file_1_output_of_rs), .Output_of_rt(register_file_1_output_of_rt),
    .Write_Data(multiplexer_2_out));
  ALU alu_1 (
    .rs(register_file_1_output_of_rs), .rt(register_file_1_output_of_rt), ._0_3(rom_1_data_2[3:0]),
    .Output(alu_1_output), .Opcode(rom_1_data_2[15:12]));
  Multiplexer #(.width(16), .enable("false")) multiplexer_2 (
    .in0({{8{1'b0}}, rom_1_data_3, rom_1_data_2[3:0]}), .in1(multiplexer_3_out), .out(multiplexer_2_out),
    .sel(contol_unit_1_mux2));
  Multiplexer #(.width(16), .enable("false")) multiplexer_3 (
    .in0(alu_1_output), .in1(ram_1_data), .out(multiplexer_3_out), .sel(contol_unit_1_mux1));
  RAM #(.dataWidth(16), .bus("separate")) ram_1 (
    .addr({rom_1_data_3, rom_1_data_2[3:0]}), .din(register_file_1_output_of_rs), .data(ram_1_data),
    .str(contol_unit_1_wmem), .sel(1'b1), .clk(clock_1_out), .ld(contol_unit_1_rmem), .clr(in_5));

  // Notes on the sheet:
  //   Instruction Memory
  //   Controller
  //   contents of rom_1 (hex, n*v repeats v):
  //   f002 f103 f205 f607 1122 c263 7302 5003
  //   Data Memory
endmodule
